# Fritzing sketch schematic-binaryclock (saved by Fritzing 0.9.2b)
breadboards: 1

parts:
  Part1 = Arduino Uno (Rev3)
  LED1 = LED - 5mm [color="Red (633nm)" package="5 mm [THT]"]
  LED2 = LED - 5mm [color="Red (633nm)" package="5 mm [THT]"]
  LED3 = LED - 5mm [color="Red (633nm)" package="5 mm [THT]"]
  LED4 = LED - 5mm [color="Red (633nm)" package="5 mm [THT]"]
  LED5 = LED - 5mm [color="Red (633nm)" package="5 mm [THT]"]
  LED12 = LED - 5mm [color="Yellow (585nm)" package="5 mm [THT]"]
  LED7 = LED - 5mm [color="Yellow (585nm)" package="5 mm [THT]"]
  LED8 = LED - 5mm [color="Yellow (585nm)" package="5 mm [THT]"]
  LED9 = LED - 5mm [color="Yellow (585nm)" package="5 mm [THT]"]
  LED10 = LED - 5mm [color="Yellow (585nm)" package="5 mm [THT]"]
  LED11 = LED - 5mm [color="Yellow (585nm)" package="5 mm [THT]"]
  LED18 = LED - 5mm [color="Green (565nm)" package="5 mm [THT]"]
  LED13 = LED - 5mm [color="Green (565nm)" package="5 mm [THT]"]
  LED14 = LED - 5mm [color="Green (565nm)" package="5 mm [THT]"]
  LED15 = LED - 5mm [color="Green (565nm)" package="5 mm [THT]"]
  LED16 = LED - 5mm [color="Green (565nm)" package="5 mm [THT]"]
  LED17 = LED - 5mm [color="Green (565nm)" package="5 mm [THT]"]
  LED6 = LED - 5mm [color="Red (633nm)" package="5 mm [THT]"]
  R1 = Resistor [tolerance=±5% resistance=150 package=THT]
  R2 = Resistor [tolerance=±5% resistance=150 package=THT]
  R3 = Resistor [tolerance=±5% resistance=150 package=THT]
  R4 = Resistor [tolerance=±5% resistance=150 package=THT]
  R5 = Resistor [tolerance=±5% resistance=150 package=THT]
  LED19 = LED - 5mm [color="Green (565nm)" package="5 mm [THT]"]
  LED20 = LED - 5mm [color="Green (565nm)" package="5 mm [THT]"]

nets:
  N1: Part1.D2, LED5.anode, LED9.anode, LED13.anode, LED17.anode, R1.Pin_0
  N2: Part1.D3_PWM, LED1.anode, LED10.anode, LED18.anode, LED14.anode, R2.Pin_0
  N3: Part1.D4, LED2.anode, LED15.anode, LED6.anode, R3.Pin_0, LED19.anode
  N4: Part1.D5_PWM, LED3.anode, LED7.anode, LED11.anode, R4.Pin_0, LED20.anode
  N5: Part1.D6_PWM, LED4.anode, LED12.anode, LED8.anode, LED16.anode, R5.Pin_0
  N6: LED1.cathode, LED2.cathode, LED3.cathode, LED4.cathode, R1.Pin_1
  N7: LED5.cathode, LED7.cathode, LED8.cathode, LED6.cathode, R2.Pin_1
  N8: LED12.cathode, LED9.cathode, LED10.cathode, LED11.cathode, R3.Pin_1
  N9: LED18.cathode, LED17.cathode, R5.Pin_1, LED19.cathode, LED20.cathode
  N10: LED13.cathode, LED14.cathode, LED15.cathode, LED16.cathode, R4.Pin_1
